# Fritzing sketch sketch (saved by Fritzing 0.9.10b)

parts:
  U1 = ESP32S-HiLetgo [part_number=ESP32S-HiLetgo]
  Componente1 = InvenSense MPU6050
  U2 = LIPO-1000mAh [package=lipo-1000]
  Componente2 = QMC5883L - Triple Axis Magnetometer Breakout
  M1 = MT3608 Module
  U3 = L9110 H-bridge module [part_number="L9110 H-bridge"]
  M2 = DC Motor [voltage_(max)=6V voltage_(min)=3V]
  M3 = DC Motor [voltage_(max)=6V voltage_(min)=3V]

nets:
  N1: U1.3.3, Componente2.VCC
  N2: U1.VIN, M1.pin3
  N3: U1.GPIO0, U3.A-IA
  N4: U1.GPIO4, U3.B-IA
  N5: U1.GPIO21, Componente2.SDA
  N6: U1.GPIO22, Componente2.SCL
  N7: Componente1.GND, Componente1.SCL
  N8: U2.+, M1.pin2
  N9: U2.-, M1.pin1
  N10: U3.MOTOR_A-A, M3.pin_2
  N11: U3.MOTOR_A-B, M3.pin_1
  N12: U3.MOTOR_B-A, M2.pin_2
  N13: U3.MOTOR_B-B, M2.pin_1

custom parts:
  ESP32S-HiLetgo: HiLetgo ESP-WROOM-32 ESP32 ESP-32S Development Board 2.4GHz Dual-Mode WiFi + Bluetooth Dual Cores Microcontroller The ESP32 integrated with Antenna switches, RF Balun, power amplifiers, low-noise amplifiers, filters, and management modules, and the entire solution occupies the least area of PCB. 2.4 GHz Wi-Fi plus Bluetooth dual-mode chip, with TSMC Ultra-low power consumption 40nm technology,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
  MT3608 Module: MT3608 Boost Converter Module Links: Aerosemi MT3608 2A Step Up Converter datasheet
